// Logisim project educpu.circ as structural Verilog: 11 circuits, main circuit main
module main (
  input  RESET
);

  wire alu_1_c_b_out, alu_1_eq, alu_1_lt, and_1_out, and_2_out, and_3_out, and_4_out, and_5_out, and_6_out,
       and_7_out, and_8_out, and_9_out, and_10_out, and_11_out, and_12_out, and_14_out, and_15_out,
       branchcontrol_1_execute, comparator_1_eq, comparator_2_eq, comparator_3_eq, comparator_4_eq,
       comparator_5_eq, comparator_6_eq, comparator_7_eq, comparator_8_eq, comparator_9_eq, comparator_10_eq,
       comparator_11_eq, comparator_12_eq, comparator_13_eq, comparator_14_eq, comparator_15_eq,
       comparator_16_eq, comparator_17_eq, comparator_18_eq, comparator_19_eq, comparator_20_eq,
       comparator_21_eq, comparator_22_eq, comparator_23_eq, comparator_24_eq, MCLK, MWRITE, not_1_out,
       opcodedecoder_1_addcmem, opcodedecoder_1_addmem, opcodedecoder_1_com, opcodedecoder_1_is_arith,
       opcodedecoder_1_subbmem, opcodedecoder_1_submem, opcodedecoder_2_strmem, opcodedecoder_3_load_mem,
       opcodedecoder_4_terminate, opcodedecoder_4_write, opcodedecoder_5_ldimm, opcodedecoder_5_ldmem,
       opcodedecoder_6_jmp, opcodedecoder_6_jmpeq, opcodedecoder_6_jmplt, opcodedecoder_6_jmpneq, or_1_out,
       or_2_out, or_3_out, or_4_out, or_5_out, or_6_out, or_7_out, or_8_out, or_9_out, or_10_out, or_11_out,
       or_12_out, or_13_out, or_14_out, or_15_out, RCLK, RUN, srdecoder_1_car_bor, TERMINATE, TTYCLK,
       WE_ACCU, WE_INSN, WE_PC, WE_SR;
  wire [7:0] ACC, ACC_next, alu_1_result, CLK, DATA, insndecoder_1_opcode, insndecoder_1_operand_lo,
       insndecoder_2_opcode, insndecoder_3_opcode, insndecoder_4_opcode, insndecoder_5_opcode,
       insndecoder_5_operand_lo, insndecoder_6_opcode, SR, SR_next, srencoder_1_sr, TTYDATA;
  wire [15:0] ADDR, inc16_1_outval, inc16_2_outval, inc16_3_outval, insndecoder_2_operand,
       insndecoder_3_operand, insndecoder_6_operand, PC, PC_next;
  wire [23:0] INSN, INSN_next, set8of24_1_outval, set8of24_2_outval, set8of24_3_outval, set8of24_4_outval;

  // Probe on ADDR
  Comparator comparator_1 (.a(CLK), .b(8'h1), .eq(comparator_1_eq));  // open: gt, lt
  Comparator comparator_2 (.a(CLK), .b(8'h2), .eq(comparator_2_eq));  // open: gt, lt
  Comparator comparator_3 (.a(CLK), .b(8'h3), .eq(comparator_3_eq));  // open: gt, lt
  ClockGenerator clockgenerator_1 (.RESET(RESET), .ENABLE(RUN), .CLK(CLK));
  // Probe on DATA
  assign ADDR = or_1_out ? PC : 16'bz;  // Controlled_Buffer controlled_buffer_1
  or or_1 (or_1_out, comparator_1_eq, comparator_2_eq, comparator_3_eq);
  or or_2 (or_2_out, comparator_2_eq, comparator_3_eq);
  assign RCLK = comparator_3_eq ? 1'b1 : 1'bz;  // Controlled_Buffer controlled_buffer_2
  InsnDecoder insndecoder_1 (
    .INSN(INSN), .OPERAND_LO(insndecoder_1_operand_lo), .OPCODE(insndecoder_1_opcode));  // open: OPERAND, OPERAND_HI
  Pull_Resistor pull_resistor_1 (.node(ADDR));
  Pull_Resistor pull_resistor_2 (.node(MCLK));
  assign WE_PC = or_2_out ? 1'b1 : 1'bz;  // Controlled_Buffer controlled_buffer_3
  assign WE_INSN = or_2_out ? 1'b1 : 1'bz;  // Controlled_Buffer controlled_buffer_4
  assign MCLK = or_2_out ? 1'b1 : 1'bz;  // Controlled_Buffer controlled_buffer_5
  not not_1 (not_1_out, MWRITE);
  Pull_Resistor pull_resistor_3 (.node(MWRITE));
  Pull_Resistor pull_resistor_4 (.node(TERMINATE));
  // Probe on CLK
  // Probe on PC
  // Probe on INSN
  // Probe on ACC
  assign PC_next = or_1_out ? inc16_1_outval : 16'bz;  // Controlled_Buffer controlled_buffer_6
  Inc16 inc16_1 (.INVAL(PC), .OUTVAL(inc16_1_outval));
  RAM #(.addrWidth(16), .databus("bidir")) ram_1 (.addr(ADDR), .we(MWRITE), .oe(not_1_out), .clk(MCLK), .data(DATA));
  S_R_Flip_Flop #(.trigger("high")) s_r_ff_1 (
    .S(RESET), .R(TERMINATE), .clk(1'b1), .Q(RUN));  // open: reset, Qn, preset
  Set8of24 set8of24_1 (.INVAL(INSN), .REPLACE(DATA), .INDEX(2'b10), .OUTVAL(set8of24_1_outval));
  Comparator comparator_4 (.a(CLK), .b(8'h10), .eq(comparator_4_eq));  // open: gt, lt
  Comparator comparator_5 (.a(CLK), .b(8'h11), .eq(comparator_5_eq));  // open: gt, lt
  assign INSN_next = or_1_out ? set8of24_1_outval : 24'bz;  // Controlled_Buffer controlled_buffer_7
  and and_1 (and_1_out, opcodedecoder_1_is_arith, comparator_4_eq);
  and and_2 (and_2_out, opcodedecoder_1_is_arith, comparator_5_eq);
  OpcodeDecoder opcodedecoder_1 (
    .OPCODE(insndecoder_1_opcode), .ADDMEM(opcodedecoder_1_addmem), .ADDCMEM(opcodedecoder_1_addcmem),
    .SUBMEM(opcodedecoder_1_submem), .SUBBMEM(opcodedecoder_1_subbmem), .COM(opcodedecoder_1_com),
    .IS_ARITH(opcodedecoder_1_is_arith));  // open: NOP, LDIMM, LDMEM, STRMEM, JMP, JMPEQ, JMPNEQ, JMPLT, LOAD_MEM, WRITE, TERMINATE
  Comparator comparator_6 (.a(CLK), .b(8'h4), .eq(comparator_6_eq));  // open: gt, lt
  Comparator comparator_7 (.a(CLK), .b(8'h5), .eq(comparator_7_eq));  // open: gt, lt
  Comparator comparator_8 (.a(CLK), .b(8'h6), .eq(comparator_8_eq));  // open: gt, lt
  or or_3 (or_3_out, and_1_out, and_2_out);
  assign RCLK = and_2_out ? 1'b1 : 1'bz;  // Controlled_Buffer controlled_buffer_8
  Pull_Resistor pull_resistor_5 (.node(TTYCLK));
  assign WE_SR = or_3_out ? 1'b1 : 1'bz;  // Controlled_Buffer controlled_buffer_9
  assign WE_ACCU = or_3_out ? 1'b1 : 1'bz;  // Controlled_Buffer controlled_buffer_10
  assign ADDR = or_4_out ? PC : 16'bz;  // Controlled_Buffer controlled_buffer_11
  or or_4 (or_4_out, comparator_6_eq, comparator_7_eq, comparator_8_eq);
  or or_5 (or_5_out, comparator_7_eq, comparator_8_eq);
  assign RCLK = comparator_8_eq ? 1'b1 : 1'bz;  // Controlled_Buffer controlled_buffer_12
  assign WE_PC = or_5_out ? 1'b1 : 1'bz;  // Controlled_Buffer controlled_buffer_13
  assign WE_INSN = or_5_out ? 1'b1 : 1'bz;  // Controlled_Buffer controlled_buffer_14
  assign MCLK = or_5_out ? 1'b1 : 1'bz;  // Controlled_Buffer controlled_buffer_15
  TTY tty_1 (.data(TTYDATA[6:0]), .clk(TTYCLK), .clr(RESET));  // open: we
  assign PC_next = or_4_out ? inc16_2_outval : 16'bz;  // Controlled_Buffer controlled_buffer_16
  Inc16 inc16_2 (.INVAL(PC), .OUTVAL(inc16_2_outval));
  Registers registers_1 (
    .ACC(ACC), .INSN(INSN), .PC(PC), .SR(SR), .WE_INSN(WE_INSN), .INSN_next(INSN_next), .RESET(RESET),
    .CLK(RCLK), .WE_PC(WE_PC), .PC_next(PC_next), .SR_next(SR_next), .WE_SR(WE_SR), .ACC_Next(ACC_next),
    .WE_ACC(WE_ACCU));
  Set8of24 set8of24_2 (.INVAL(INSN), .REPLACE(DATA), .INDEX(2'b01), .OUTVAL(set8of24_2_outval));
  assign INSN_next = or_4_out ? set8of24_2_outval : 24'bz;  // Controlled_Buffer controlled_buffer_17
  ALU alu_1 (
    .RESULT(alu_1_result), .C_B_OUT(alu_1_c_b_out), .EQ(alu_1_eq), .LT(alu_1_lt),
    .C_B_IN(srdecoder_1_car_bor), .ADD(opcodedecoder_1_addmem), .ADDC(opcodedecoder_1_addcmem),
    .SUB(opcodedecoder_1_submem), .SUBB(opcodedecoder_1_subbmem), .COM(opcodedecoder_1_com), .OP1(ACC),
    .OP2(insndecoder_1_operand_lo));
  SRDecoder srdecoder_1 (.SR(SR), .CAR_BOR(srdecoder_1_car_bor));  // open: EQ, LT
  assign ACC_next = or_3_out ? alu_1_result : 8'bz;  // Controlled_Buffer controlled_buffer_18
  Comparator comparator_9 (.a(CLK), .b(8'h7), .eq(comparator_9_eq));  // open: gt, lt
  Comparator comparator_10 (.a(CLK), .b(8'h8), .eq(comparator_10_eq));  // open: gt, lt
  Comparator comparator_11 (.a(CLK), .b(8'h9), .eq(comparator_11_eq));  // open: gt, lt
  SREncoder srencoder_1 (.CAR_BOR(alu_1_c_b_out), .EQ(alu_1_eq), .LT(alu_1_lt), .SR(srencoder_1_sr));
  assign SR_next = or_3_out ? srencoder_1_sr : 8'bz;  // Controlled_Buffer controlled_buffer_19
  assign ADDR = or_6_out ? PC : 16'bz;  // Controlled_Buffer controlled_buffer_20
  or or_6 (or_6_out, comparator_9_eq, comparator_10_eq, comparator_11_eq);
  or or_7 (or_7_out, comparator_10_eq, comparator_11_eq);
  assign RCLK = comparator_11_eq ? 1'b1 : 1'bz;  // Controlled_Buffer controlled_buffer_21
  assign WE_PC = or_7_out ? 1'b1 : 1'bz;  // Controlled_Buffer controlled_buffer_22
  assign WE_INSN = or_7_out ? 1'b1 : 1'bz;  // Controlled_Buffer controlled_buffer_23
  assign MCLK = or_7_out ? 1'b1 : 1'bz;  // Controlled_Buffer controlled_buffer_24
  assign PC_next = or_6_out ? inc16_3_outval : 16'bz;  // Controlled_Buffer controlled_buffer_25
  Inc16 inc16_3 (.INVAL(PC), .OUTVAL(inc16_3_outval));
  Set8of24 set8of24_3 (.INVAL(INSN), .REPLACE(DATA), .INDEX(2'b00), .OUTVAL(set8of24_3_outval));
  assign INSN_next = or_6_out ? set8of24_3_outval : 24'bz;  // Controlled_Buffer controlled_buffer_26
  InsnDecoder insndecoder_2 (
    .INSN(INSN), .OPERAND(insndecoder_2_operand), .OPCODE(insndecoder_2_opcode));  // open: OPERAND_LO, OPERAND_HI
  Comparator comparator_12 (.a(CLK), .b(8'h12), .eq(comparator_12_eq));  // open: gt, lt
  Comparator comparator_13 (.a(CLK), .b(8'h13), .eq(comparator_13_eq));  // open: gt, lt
  and and_3 (and_3_out, opcodedecoder_2_strmem, comparator_12_eq);
  and and_4 (and_4_out, opcodedecoder_2_strmem, comparator_13_eq);
  OpcodeDecoder opcodedecoder_2 (
    .OPCODE(insndecoder_2_opcode), .STRMEM(opcodedecoder_2_strmem));  // open: NOP, LDIMM, LDMEM, JMP, JMPEQ, JMPNEQ, JMPLT, ADDMEM, ADDCMEM, SUBMEM, SUBBMEM, LOAD_MEM, COM, IS_ARITH, WRITE, TERMINATE
  InsnDecoder insndecoder_3 (
    .INSN(INSN), .OPERAND(insndecoder_3_operand), .OPCODE(insndecoder_3_opcode));  // open: OPERAND_LO, OPERAND_HI
  or or_8 (or_8_out, and_3_out, and_4_out);
  assign MCLK = and_4_out ? 1'b1 : 1'bz;  // Controlled_Buffer controlled_buffer_27
  assign MWRITE = or_8_out ? 1'b1 : 1'bz;  // Controlled_Buffer controlled_buffer_28
  Comparator comparator_14 (.a(CLK), .b(8'ha), .eq(comparator_14_eq));  // open: gt, lt
  Comparator comparator_15 (.a(CLK), .b(8'hb), .eq(comparator_15_eq));  // open: gt, lt
  Comparator comparator_16 (.a(CLK), .b(8'hc), .eq(comparator_16_eq));  // open: gt, lt
  Comparator comparator_17 (.a(CLK), .b(8'hd), .eq(comparator_17_eq));  // open: gt, lt
  and and_5 (and_5_out, opcodedecoder_3_load_mem, comparator_14_eq);
  and and_6 (and_6_out, opcodedecoder_3_load_mem, comparator_15_eq);
  and and_7 (and_7_out, opcodedecoder_3_load_mem, comparator_16_eq);
  and and_8 (and_8_out, opcodedecoder_3_load_mem, comparator_17_eq);
  assign ADDR = or_8_out ? insndecoder_2_operand : 16'bz;  // Controlled_Buffer controlled_buffer_29
  assign DATA = or_8_out ? ACC : 8'bz;  // Controlled_Buffer controlled_buffer_30
  OpcodeDecoder opcodedecoder_3 (
    .OPCODE(insndecoder_3_opcode), .LOAD_MEM(opcodedecoder_3_load_mem));  // open: NOP, LDIMM, LDMEM, STRMEM, JMP, JMPEQ, JMPNEQ, JMPLT, ADDMEM, ADDCMEM, SUBMEM, SUBBMEM, COM, IS_ARITH, WRITE, TERMINATE
  or or_9 (or_9_out, and_5_out, and_6_out, and_7_out, and_8_out);
  or or_10 (or_10_out, and_6_out, and_7_out, and_8_out);
  or or_11 (or_11_out, and_7_out, and_8_out);
  assign MCLK = or_10_out ? 1'b1 : 1'bz;  // Controlled_Buffer controlled_buffer_31
  assign WE_INSN = or_11_out ? 1'b1 : 1'bz;  // Controlled_Buffer controlled_buffer_32
  assign RCLK = and_8_out ? 1'b1 : 1'bz;  // Controlled_Buffer controlled_buffer_33
  assign ADDR = or_9_out ? insndecoder_3_operand : 16'bz;  // Controlled_Buffer controlled_buffer_34
  InsnDecoder insndecoder_4 (.INSN(INSN), .OPCODE(insndecoder_4_opcode));  // open: OPERAND, OPERAND_LO, OPERAND_HI
  Set8of24 set8of24_4 (.INVAL(INSN), .REPLACE(DATA), .INDEX(2'b00), .OUTVAL(set8of24_4_outval));
  assign INSN_next = or_11_out ? set8of24_4_outval : 24'bz;  // Controlled_Buffer controlled_buffer_35
  Comparator comparator_18 (.a(CLK), .b(8'h14), .eq(comparator_18_eq));  // open: gt, lt
  Comparator comparator_19 (.a(CLK), .b(8'h15), .eq(comparator_19_eq));  // open: gt, lt
  and and_9 (and_9_out, opcodedecoder_4_write, comparator_18_eq);
  and and_10 (and_10_out, opcodedecoder_4_write, comparator_19_eq);
  InsnDecoder insndecoder_5 (
    .INSN(INSN), .OPERAND_LO(insndecoder_5_operand_lo), .OPCODE(insndecoder_5_opcode));  // open: OPERAND, OPERAND_HI
  OpcodeDecoder opcodedecoder_4 (
    .OPCODE(insndecoder_4_opcode), .WRITE(opcodedecoder_4_write), .TERMINATE(opcodedecoder_4_terminate));  // open: NOP, LDIMM, LDMEM, STRMEM, JMP, JMPEQ, JMPNEQ, JMPLT, ADDMEM, ADDCMEM, SUBMEM, SUBBMEM, LOAD_MEM, COM, IS_ARITH
  or or_12 (or_12_out, and_9_out, and_10_out);
  assign TTYDATA = or_12_out ? ACC : 8'bz;  // Controlled_Buffer controlled_buffer_36
  assign TTYCLK = and_10_out ? 1'b1 : 1'bz;  // Controlled_Buffer controlled_buffer_37
  Comparator comparator_20 (.a(CLK), .b(8'he), .eq(comparator_20_eq));  // open: gt, lt
  Comparator comparator_21 (.a(CLK), .b(8'hf), .eq(comparator_21_eq));  // open: gt, lt
  and and_11 (and_11_out, or_14_out, comparator_20_eq);
  and and_12 (and_12_out, or_14_out, comparator_21_eq);
  Comparator comparator_22 (.a(CLK), .b(8'h14), .eq(comparator_22_eq));  // open: gt, lt
  OpcodeDecoder opcodedecoder_5 (
    .OPCODE(insndecoder_5_opcode), .LDIMM(opcodedecoder_5_ldimm), .LDMEM(opcodedecoder_5_ldmem));  // open: NOP, STRMEM, JMP, JMPEQ, JMPNEQ, JMPLT, ADDMEM, ADDCMEM, SUBMEM, SUBBMEM, LOAD_MEM, COM, IS_ARITH, WRITE, TERMINATE
  or or_13 (or_13_out, and_11_out, and_12_out);
  assign RCLK = and_12_out ? 1'b1 : 1'bz;  // Controlled_Buffer controlled_buffer_38
  and and_13 (TERMINATE, opcodedecoder_4_terminate, comparator_22_eq);
  or or_14 (or_14_out, opcodedecoder_5_ldimm, opcodedecoder_5_ldmem);
  assign WE_ACCU = or_13_out ? 1'b1 : 1'bz;  // Controlled_Buffer controlled_buffer_39
  assign ACC_next = or_13_out ? insndecoder_5_operand_lo : 8'bz;  // Controlled_Buffer controlled_buffer_40
  InsnDecoder insndecoder_6 (
    .INSN(INSN), .OPERAND(insndecoder_6_operand), .OPCODE(insndecoder_6_opcode));  // open: OPERAND_LO, OPERAND_HI
  Comparator comparator_23 (.a(CLK), .b(8'h16), .eq(comparator_23_eq));  // open: gt, lt
  Comparator comparator_24 (.a(CLK), .b(8'h17), .eq(comparator_24_eq));  // open: gt, lt
  and and_14 (and_14_out, branchcontrol_1_execute, comparator_23_eq);
  and and_15 (and_15_out, branchcontrol_1_execute, comparator_24_eq);
  OpcodeDecoder opcodedecoder_6 (
    .OPCODE(insndecoder_6_opcode), .JMP(opcodedecoder_6_jmp), .JMPEQ(opcodedecoder_6_jmpeq),
    .JMPNEQ(opcodedecoder_6_jmpneq), .JMPLT(opcodedecoder_6_jmplt));  // open: NOP, LDIMM, LDMEM, STRMEM, ADDMEM, ADDCMEM, SUBMEM, SUBBMEM, LOAD_MEM, COM, IS_ARITH, WRITE, TERMINATE
  or or_15 (or_15_out, and_14_out, and_15_out);
  assign PC_next = or_15_out ? insndecoder_6_operand : 16'bz;  // Controlled_Buffer controlled_buffer_41
  assign WE_PC = or_15_out ? 1'b1 : 1'bz;  // Controlled_Buffer controlled_buffer_42
  assign RCLK = and_15_out ? 1'b1 : 1'bz;  // Controlled_Buffer controlled_buffer_43
  BranchControl branchcontrol_1 (
    .SR(SR), .JMP(opcodedecoder_6_jmp), .JMPEQ(opcodedecoder_6_jmpeq), .JMPNEQ(opcodedecoder_6_jmpneq),
    .JMPLT(opcodedecoder_6_jmplt), .EXECUTE(branchcontrol_1_execute));

  // Notes on the sheet:
  //   Clock 1 2 3: Load Opcode
  //   Clock 16 17: Execute ALU
  //   Clock 4 5 6: Load high operand
  //   Clock 7 8 9: Load low operand
  //   Clock 18 19: Execute store instructions
  //   Clock 10 11 12 13: Execute load from memory
  //   Clock 20 21: Execute write/terminate
  //   Clock 14 15: Finalize load instructions
  //   Clock 22 23: Execute jump
endmodule

module Registers (
  input  [15:0] PC_next,
  input  [7:0] SR_next,
  input  [7:0] ACC_Next,
  input  [23:0] INSN_next,
  input  RESET,
  input  CLK,
  input  WE_PC,
  input  WE_SR,
  input  WE_ACC,
  input  WE_INSN,
  output [15:0] PC,
  output [7:0] SR,
  output [7:0] ACC,
  output [23:0] INSN
);

  Register #(.width(16)) Reg_PC (.D(PC_next), .en(WE_PC), .clk(CLK), .Q(PC), .clr(RESET));
  Register Reg_SR (.D(SR_next), .en(WE_SR), .clk(CLK), .Q(SR), .clr(RESET));
  Register register_1 (.D(ACC_Next), .en(WE_ACC), .clk(CLK), .Q(ACC), .clr(RESET));
  Register #(.width(24)) register_2 (.D(INSN_next), .en(WE_INSN), .clk(CLK), .Q(INSN), .clr(RESET));

  // Notes on the sheet:
  //   WE_INSN: pull=down
  //   WE_PC: pull=down
  //   WE_SR: pull=down
  //   WE_ACC: pull=down
endmodule

module ClockGenerator (
  input  RESET,
  input  ENABLE,
  output [7:0] CLK
);

  wire and_1_out, clock_1_out;

  Clock clock_1 (.out(clock_1_out));
  and and_1 (and_1_out, clock_1_out, ENABLE);
  Counter #(.max('h17)) counter_1 (.clr(RESET), .load(1'b0), .clk(and_1_out), .Q(CLK));  // open: up, count, D, carry
endmodule

module Inc16 (
  input  [15:0] INVAL,
  output [15:0] OUTVAL
);

  Adder #(.width(16)) adder_1 (.a(INVAL), .b({16{1'b0}}), .out(OUTVAL), .cin(1'b1));  // open: cout
endmodule

module Set8of24 (
  input  [23:0] INVAL,
  input  [7:0] REPLACE,
  input  [1:0] INDEX,
  output [23:0] OUTVAL
);

  wire and_1_out, and_2_out, and_3_out;

  and and_1 (and_1_out, ~INDEX[0], ~INDEX[1]);  // AND_Gate
  and and_2 (and_2_out, INDEX[0], ~INDEX[1]);  // AND_Gate
  and and_3 (and_3_out, ~INDEX[0], INDEX[1]);  // AND_Gate
  Multiplexer #(.width(8)) multiplexer_1 (.in0(INVAL[7:0]), .in1(REPLACE), .out(OUTVAL[7:0]), .sel(and_1_out));
  Multiplexer #(.width(8)) multiplexer_2 (.in0(INVAL[15:8]), .in1(REPLACE), .out(OUTVAL[15:8]), .sel(and_2_out));
  Multiplexer #(.width(8)) multiplexer_3 (.in0(INVAL[23:16]), .in1(REPLACE), .out(OUTVAL[23:16]), .sel(and_3_out));
endmodule

module InsnDecoder (
  input  [23:0] INSN,
  output [15:0] OPERAND,
  output [7:0] OPERAND_LO,
  output [7:0] OPERAND_HI,
  output [7:0] OPCODE
);


  assign OPCODE = INSN[23:16];
  assign OPERAND = INSN[15:0];
  assign OPERAND_HI = INSN[15:8];
  assign OPERAND_LO = INSN[7:0];
endmodule

module OpcodeDecoder (
  input  [7:0] OPCODE,
  output NOP,
  output LDIMM,
  output LDMEM,
  output STRMEM,
  output JMP,
  output JMPEQ,
  output JMPNEQ,
  output JMPLT,
  output ADDMEM,
  output ADDCMEM,
  output SUBMEM,
  output SUBBMEM,
  output LOAD_MEM,
  output COM,
  output IS_ARITH,
  output WRITE,
  output TERMINATE
);

  Comparator comparator_1 (.a(OPCODE), .b({8{1'b0}}), .eq(NOP));  // open: gt, lt
  Comparator comparator_2 (.a(OPCODE), .b(8'h1), .eq(LDIMM));  // open: gt, lt
  Comparator comparator_3 (.a(OPCODE), .b(8'h2), .eq(LDMEM));  // open: gt, lt
  Comparator comparator_4 (.a(OPCODE), .b(8'h3), .eq(STRMEM));  // open: gt, lt
  Comparator comparator_5 (.a(OPCODE), .b(8'h4), .eq(JMP));  // open: gt, lt
  Comparator comparator_6 (.a(OPCODE), .b(8'h5), .eq(JMPEQ));  // open: gt, lt
  Comparator comparator_7 (.a(OPCODE), .b(8'h6), .eq(JMPNEQ));  // open: gt, lt
  Comparator comparator_8 (.a(OPCODE), .b(8'h7), .eq(JMPLT));  // open: gt, lt
  Comparator comparator_9 (.a(OPCODE), .b(8'h8), .eq(ADDMEM));  // open: gt, lt
  Comparator comparator_10 (.a(OPCODE), .b(8'h9), .eq(ADDCMEM));  // open: gt, lt
  Comparator comparator_11 (.a(OPCODE), .b(8'ha), .eq(SUBMEM));  // open: gt, lt
  Comparator comparator_12 (.a(OPCODE), .b(8'hb), .eq(SUBBMEM));  // open: gt, lt
  Comparator comparator_13 (.a(OPCODE), .b(8'hc), .eq(COM));  // open: gt, lt
  Comparator comparator_14 (.a(OPCODE), .b(8'hd), .eq(WRITE));  // open: gt, lt
  Comparator comparator_15 (.a(OPCODE), .b(8'he), .eq(TERMINATE));  // open: gt, lt
  or or_1 (LOAD_MEM, ADDMEM, ADDCMEM, SUBMEM, SUBBMEM, LDMEM);
  or or_2 (IS_ARITH, ADDMEM, ADDCMEM, SUBMEM, SUBBMEM, COM);
endmodule

module ALU (
  input  C_B_IN,
  input  ADD,
  input  ADDC,
  input  SUB,
  input  SUBB,
  input  COM,
  input  [7:0] OP1,
  input  [7:0] OP2,
  output C_B_OUT,
  output [7:0] RESULT,
  output EQ,
  output LT
);

  wire adder_1_cout, and_1_out, and_2_out, and_3_out, or_1_out, or_2_out, or_3_out, subtractor_1_bout;
  wire [1:0] priority_encoder_1_out;
  wire [7:0] adder_1_out, not_1_out, subtractor_1_out;

  or or_1 (or_1_out, ADD, ADDC);
  or or_2 (or_2_out, SUB, SUBB);
  or or_3 (or_3_out, ADDC, SUBB);
  and and_1 (and_1_out, or_3_out, C_B_IN);
  assign not_1_out = ~OP1;  // NOT_Gate not_1, 8 bits wide
  Comparator comparator_1 (.a(OP2), .b(OP1), .eq(EQ), .lt(LT));  // open: gt
  Adder adder_1 (.a(OP1), .b(OP2), .out(adder_1_out), .cin(and_1_out), .cout(adder_1_cout));
  Subtractor subtractor_1 (.a(OP1), .b(OP2), .out(subtractor_1_out), .bin(and_1_out), .bout(subtractor_1_bout));
  Priority_Encoder #(.select(2)) priority_encoder_1 (
    .in0(or_1_out), .in1(or_2_out), .in2(COM), .out(priority_encoder_1_out));  // open: in3, gs, en_out, en_in
  Multiplexer #(.select(2), .width(8)) multiplexer_1 (
    .in0(adder_1_out), .in1(subtractor_1_out), .in2(not_1_out), .out(RESULT), .sel(priority_encoder_1_out));  // open: in3
  and and_2 (and_2_out, or_1_out, adder_1_cout);
  and and_3 (and_3_out, or_2_out, subtractor_1_bout);
  or or_4 (C_B_OUT, and_2_out, and_3_out);
endmodule

module SRDecoder (
  input  [7:0] SR,
  output CAR_BOR,
  output EQ,
  output LT
);


  assign CAR_BOR = SR[0];
  assign EQ = SR[1];
  assign LT = SR[2];
endmodule

module SREncoder (
  input  CAR_BOR,
  input  EQ,
  input  LT,
  output [7:0] SR
);


  assign SR = {{5{1'b0}}, LT, EQ, CAR_BOR};
endmodule

module BranchControl (
  input  [7:0] SR,
  input  JMP,
  input  JMPEQ,
  input  JMPNEQ,
  input  JMPLT,
  output EXECUTE
);

  wire and_1_out, and_2_out, and_3_out, srdecoder_1_eq, srdecoder_1_lt;

  SRDecoder srdecoder_1 (.SR(SR), .EQ(srdecoder_1_eq), .LT(srdecoder_1_lt));  // open: CAR_BOR
  and and_1 (and_1_out, srdecoder_1_eq, JMPEQ);
  and and_2 (and_2_out, ~srdecoder_1_eq, JMPNEQ);  // AND_Gate
  and and_3 (and_3_out, srdecoder_1_lt, JMPLT);
  or or_1 (EXECUTE, JMP, and_1_out, and_2_out, and_3_out);
endmodule
